// Logisim project 模8计数器.circ as structural Verilog: 1 circuit, main circuit main
module main (
  input  in_1
);

  wire and_1_out, j_k_ff_1_q, j_k_ff_2_q, j_k_ff_3_q, undriven, undriven_2;

  J_K_Flip_Flop j_k_ff_1 (
    .J(in_1), .clk(undriven), .K(in_1), .Q(j_k_ff_1_q), .en(undriven_2));  // open: Qn, preset, reset
  J_K_Flip_Flop j_k_ff_2 (
    .J(j_k_ff_1_q), .clk(undriven), .K(j_k_ff_1_q), .Q(j_k_ff_2_q), .en(undriven_2));  // open: Qn, preset, reset
  and and_1 (and_1_out, j_k_ff_1_q, j_k_ff_2_q);
  J_K_Flip_Flop j_k_ff_3 (
    .J(and_1_out), .clk(undriven), .K(and_1_out), .Q(j_k_ff_3_q), .en(undriven_2));  // open: Qn, preset, reset

  // Notes on the sheet:
  //   CLK
  //   RST_n
  //   Q0
  //   Q1
  //   Q2
endmodule
